// Digital circuit 744040.dig as structural Verilog
module _744040 (
  input  nCP,
  input  MR,
  output Q0,
  output Q1,
  output Q2,
  output Q3,
  output Q4,
  output Q5,
  output Q6,
  output Q7,
  output Q8,
  output Q9,
  output Q10,
  output Q11
);

  wire d_ff_as_1_nq, d_ff_as_2_nq, d_ff_as_3_nq, d_ff_as_4_nq, d_ff_as_5_nq, d_ff_as_6_nq, d_ff_as_7_nq,
       d_ff_as_8_nq, d_ff_as_9_nq, d_ff_as_10_nq, d_ff_as_11_nq, d_ff_as_12_nq;

  D_FF_AS d_ff_as_1 (.Set(1'b0), .D(d_ff_as_1_nq), .C(~nCP), .Clr(MR), .Q(Q0), .nQ(d_ff_as_1_nq));
  D_FF_AS d_ff_as_2 (.Set(1'b0), .D(d_ff_as_2_nq), .C(~Q0), .Clr(MR), .Q(Q1), .nQ(d_ff_as_2_nq));
  D_FF_AS d_ff_as_3 (.Set(1'b0), .D(d_ff_as_3_nq), .C(~Q1), .Clr(MR), .Q(Q2), .nQ(d_ff_as_3_nq));
  D_FF_AS d_ff_as_4 (.Set(1'b0), .D(d_ff_as_4_nq), .C(~Q2), .Clr(MR), .Q(Q3), .nQ(d_ff_as_4_nq));
  D_FF_AS d_ff_as_5 (.Set(1'b0), .D(d_ff_as_5_nq), .C(~Q3), .Clr(MR), .Q(Q4), .nQ(d_ff_as_5_nq));
  D_FF_AS d_ff_as_6 (.Set(1'b0), .D(d_ff_as_6_nq), .C(~Q4), .Clr(MR), .Q(Q5), .nQ(d_ff_as_6_nq));
  D_FF_AS d_ff_as_7 (.Set(1'b0), .D(d_ff_as_7_nq), .C(~Q5), .Clr(MR), .Q(Q6), .nQ(d_ff_as_7_nq));
  D_FF_AS d_ff_as_8 (.Set(1'b0), .D(d_ff_as_8_nq), .C(~Q6), .Clr(MR), .Q(Q7), .nQ(d_ff_as_8_nq));
  D_FF_AS d_ff_as_9 (.Set(1'b0), .D(d_ff_as_9_nq), .C(~Q7), .Clr(MR), .Q(Q8), .nQ(d_ff_as_9_nq));
  D_FF_AS d_ff_as_10 (.Set(1'b0), .D(d_ff_as_10_nq), .C(~Q8), .Clr(MR), .Q(Q9), .nQ(d_ff_as_10_nq));
  D_FF_AS d_ff_as_11 (.Set(1'b0), .D(d_ff_as_11_nq), .C(~Q9), .Clr(MR), .Q(Q10), .nQ(d_ff_as_11_nq));
  D_FF_AS d_ff_as_12 (.Set(1'b0), .D(d_ff_as_12_nq), .C(~Q10), .Clr(MR), .Q(Q11), .nQ(d_ff_as_12_nq));
endmodule
