// Digital circuit Cmp12bits.dig as structural Verilog
module Cmp12bits (
  input  A0,
  input  A1,
  input  A2,
  input  A3,
  input  A4,
  input  A5,
  input  A6,
  input  A7,
  input  A8,
  input  A9,
  input  A10,
  input  A11,
  input  B0,
  input  B1,
  input  B2,
  input  B3,
  input  B4,
  input  B5,
  input  B6,
  input  B7,
  input  B8,
  input  B9,
  input  B10,
  input  B11,
  input  Ia_gt_b,
  input  Ia_lt_b,
  input  Ia_eq_b,
  output Oa_gt_b,
  output Oa_lt_b,
  output Oa_eq_b
);

  wire _7485_1_pin5, _7485_1_pin6, _7485_1_pin7, _7485_2_pin5, _7485_2_pin6, _7485_2_pin7;

  _7485 _7485_1 (
    .pin1(B3), .pin2(Ia_lt_b), .pin3(Ia_eq_b), .pin4(Ia_gt_b), .pin5(_7485_1_pin5), .pin6(_7485_1_pin6),
    .pin7(_7485_1_pin7), .pin8(1'b0), .pin9(B0), .pin10(A0), .pin11(B1), .pin12(A1), .pin13(A2), .pin14(B2),
    .pin15(A3), .pin16(1'b1));
  _7485 _7485_2 (
    .pin1(B7), .pin2(_7485_1_pin7), .pin3(_7485_1_pin6), .pin4(_7485_1_pin5), .pin5(_7485_2_pin5),
    .pin6(_7485_2_pin6), .pin7(_7485_2_pin7), .pin8(1'b0), .pin9(B4), .pin10(A4), .pin11(B5), .pin12(A5),
    .pin13(A6), .pin14(B6), .pin15(A7), .pin16(1'b1));
  _7485 _7485_3 (
    .pin1(B11), .pin2(_7485_2_pin7), .pin3(_7485_2_pin6), .pin4(_7485_2_pin5), .pin5(Oa_gt_b),
    .pin6(Oa_eq_b), .pin7(Oa_lt_b), .pin8(1'b0), .pin9(B8), .pin10(A8), .pin11(B9), .pin12(A9), .pin13(A10),
    .pin14(B10), .pin15(A11), .pin16(1'b1));
endmodule
