// Digital circuit DDPM_modulator.dig as structural Verilog
module DDPM_modulator (
  input  CNT_A0,
  input  CNT_A1,
  input  CNT_A2,
  input  CNT_A3,
  input  CNT_A4,
  input  CNT_A5,
  input  CNT_A6,
  input  CNT_A7,
  input  CNT_A8,
  input  CNT_A9,
  input  CNT_A10,
  input  CNT_A11,
  input  A0,
  input  A1,
  input  A2,
  input  A3,
  input  A4,
  input  A5,
  input  A6,
  input  A7,
  input  A8,
  input  A9,
  input  A10,
  input  A11,
  output DDPM
);

  wire multiplexer_1_out, multiplexer_2_out, multiplexer_3_out, multiplexer_4_out, multiplexer_5_out,
       multiplexer_6_out, multiplexer_7_out, multiplexer_8_out, multiplexer_9_out, multiplexer_10_out,
       multiplexer_11_out;

  Multiplexer multiplexer_1 (.sel(CNT_A9), .in_0(multiplexer_2_out), .in_1(A2), .out(multiplexer_1_out));
  Multiplexer multiplexer_2 (.sel(CNT_A10), .in_0(multiplexer_3_out), .in_1(A1), .out(multiplexer_2_out));
  Multiplexer multiplexer_3 (.sel(CNT_A11), .in_0(1'b0), .in_1(A0), .out(multiplexer_3_out));
  Multiplexer multiplexer_4 (.sel(CNT_A5), .in_0(multiplexer_5_out), .in_1(A6), .out(multiplexer_4_out));
  Multiplexer multiplexer_5 (.sel(CNT_A6), .in_0(multiplexer_6_out), .in_1(A5), .out(multiplexer_5_out));
  Multiplexer multiplexer_6 (.sel(CNT_A7), .in_0(multiplexer_7_out), .in_1(A4), .out(multiplexer_6_out));
  Multiplexer multiplexer_7 (.sel(CNT_A8), .in_0(multiplexer_1_out), .in_1(A3), .out(multiplexer_7_out));
  Multiplexer multiplexer_8 (.sel(CNT_A1), .in_0(multiplexer_9_out), .in_1(A10), .out(multiplexer_8_out));
  Multiplexer multiplexer_9 (.sel(CNT_A2), .in_0(multiplexer_10_out), .in_1(A9), .out(multiplexer_9_out));
  Multiplexer multiplexer_10 (.sel(CNT_A3), .in_0(multiplexer_11_out), .in_1(A8), .out(multiplexer_10_out));
  Multiplexer multiplexer_11 (.sel(CNT_A4), .in_0(multiplexer_4_out), .in_1(A7), .out(multiplexer_11_out));
  Multiplexer multiplexer_12 (.sel(CNT_A0), .in_0(multiplexer_8_out), .in_1(A11), .out(DDPM));
endmodule
