// Digital circuit DPM_Board.dig as structural Verilog
module DPM_Board (
  input  in_2,
  input  clk,
  input  in_5,
  input  in_6,
  input  in_7,
  input  in_8,
  output DPM,
  output DDPM
);

  wire _744040_1_p3, _744040_1_p4, _744040_1_p5, _744040_1_p6, wrapper12bit_1_cnt_a0, wrapper12bit_1_cnt_a1,
       wrapper12bit_1_cnt_a10, wrapper12bit_1_cnt_a11, wrapper12bit_2_cnt_a0, wrapper12bit_2_cnt_a1,
       wrapper12bit_2_cnt_a10, wrapper12bit_2_cnt_a11;

  // _744040 _744040_1: pin names not known; wires that end beside it: clk, in_2, _744040_1_p3, _744040_1_p4, _744040_1_p5, _744040_1_p6
  Wrapper12bit wrapper12bit_1 (
    .M0(1'b1), .M1(1'b0), .A0(_744040_1_p3), .A1(_744040_1_p4), .A2(1'b0), .A3(1'b0), .A4(1'b0), .A5(1'b0),
    .A6(1'b0), .A7(1'b0), .A8(1'b0), .A9(1'b0), .A10(_744040_1_p5), .A11(_744040_1_p6),
    .CNT_A0(wrapper12bit_1_cnt_a0), .CNT_A1(wrapper12bit_1_cnt_a1), .CNT_A10(wrapper12bit_1_cnt_a10),
    .CNT_A11(wrapper12bit_1_cnt_a11));  // open: CNT_A2, CNT_A3, CNT_A4, CNT_A5, CNT_A6, CNT_A7, CNT_A8, CNT_A9
  Wrapper12bit wrapper12bit_2 (
    .M0(1'b0), .M1(1'b0), .A0(_744040_1_p3), .A1(_744040_1_p4), .A2(1'b0), .A3(1'b0), .A4(1'b0), .A5(1'b0),
    .A6(1'b0), .A7(1'b0), .A8(1'b0), .A9(1'b0), .A10(_744040_1_p5), .A11(_744040_1_p6),
    .CNT_A0(wrapper12bit_2_cnt_a0), .CNT_A1(wrapper12bit_2_cnt_a1), .CNT_A10(wrapper12bit_2_cnt_a10),
    .CNT_A11(wrapper12bit_2_cnt_a11));  // open: CNT_A2, CNT_A3, CNT_A4, CNT_A5, CNT_A6, CNT_A7, CNT_A8, CNT_A9
  Cmp12bits cmp12bits_1 (
    .A0(wrapper12bit_1_cnt_a0), .A1(wrapper12bit_1_cnt_a1), .A2(wrapper12bit_1_cnt_a10),
    .A3(wrapper12bit_1_cnt_a11), .A4(1'b0), .A5(1'b0), .A6(1'b0), .A7(1'b0), .A8(1'b0), .A9(1'b0),
    .A10(1'b0), .A11(1'b0), .B0(in_5), .B1(in_6), .B2(in_7), .B3(in_8), .B4(1'b0), .B5(1'b0), .B6(1'b0),
    .B7(1'b0), .B8(1'b0), .B9(1'b0), .B10(1'b0), .B11(1'b0), .Ia_gt_b(1'b0), .Ia_lt_b(1'b0), .Ia_eq_b(1'b1),
    .Oa_lt_b(DPM));  // open: Oa_gt_b, Oa_eq_b
  DDPM_modulator ddpm_modulator_1 (
    .CNT_A0(wrapper12bit_2_cnt_a0), .CNT_A1(wrapper12bit_2_cnt_a1), .CNT_A2(wrapper12bit_2_cnt_a10),
    .CNT_A3(wrapper12bit_2_cnt_a11), .CNT_A4(1'b0), .CNT_A5(1'b0), .CNT_A6(1'b0), .CNT_A7(1'b0),
    .CNT_A8(1'b0), .CNT_A9(1'b0), .CNT_A10(1'b0), .CNT_A11(1'b0), .A0(1'b0), .A1(1'b0), .A2(1'b0), .A3(1'b0),
    .A4(1'b0), .A5(1'b0), .A6(1'b0), .A7(1'b0), .A8(in_5), .A9(in_6), .A10(in_7), .A11(in_8), .DDPM(DDPM));

  // Notes on the sheet:
  //   clk: Hz: 500
endmodule
