// Digital circuit Wrapper12bit.dig as structural Verilog
// M1  M0
// 0     0     PWM (direct)
// 0     1     DPM (croisé)
// 1     0     GRAY (gray)
// 1     1     DDPM (direct)
module Wrapper12bit (
  input  A0,
  input  A1,
  input  A2,
  input  A3,
  input  A4,
  input  A5,
  input  A6,
  input  A7,
  input  A8,
  input  A9,
  input  A10,
  input  A11,
  input  M1,
  input  M0,
  output CNT_A0,
  output CNT_A1,
  output CNT_A2,
  output CNT_A3,
  output CNT_A4,
  output CNT_A5,
  output CNT_A6,
  output CNT_A7,
  output CNT_A8,
  output CNT_A9,
  output CNT_A10,
  output CNT_A11
);

  wire and_1_out, and_2_out, and_3_out, and_4_out, and_5_out, and_6_out, and_7_out, and_8_out, and_9_out,
       and_10_out, and_11_out, and_12_out, and_13_out, and_14_out, and_15_out, and_16_out, and_17_out,
       and_18_out, and_19_out, and_20_out, and_21_out, and_22_out, and_23_out, and_24_out, and_25_out,
       and_26_out, and_27_out, and_28_out, and_29_out, and_30_out, and_31_out, and_32_out, and_33_out,
       and_34_out, and_35_out, and_36_out, and_37_out, and_38_out, and_39_out, and_40_out, or_1_out,
       xor_1_out, xor_2_out, xor_3_out, xor_4_out, xor_5_out, xor_6_out, xor_7_out, xor_8_out, xor_9_out,
       xor_10_out, xor_11_out, xor_12_out;

  and and_1 (and_1_out, ~M0, ~M1);  // And
  and and_2 (and_2_out, M0, ~M1);  // And
  and and_3 (and_3_out, ~M0, M1);  // And
  and and_4 (and_4_out, M0, M1);
  xor xor_1 (xor_1_out, A0, A1);
  xor xor_2 (xor_2_out, A1, A2);
  xor xor_3 (xor_3_out, A2, A3);
  xor xor_4 (xor_4_out, A3, A4);
  xor xor_5 (xor_5_out, A4, A5);
  xor xor_6 (xor_6_out, A5, A6);
  xor xor_7 (xor_7_out, A6, A7);
  xor xor_8 (xor_8_out, A7, A8);
  xor xor_9 (xor_9_out, A8, A9);
  xor xor_10 (xor_10_out, A9, A10);
  xor xor_11 (xor_11_out, A10, A11);
  xor xor_12 (xor_12_out, A11, 1'b0);
  or or_1 (or_1_out, and_1_out, and_4_out);
  and and_5 (and_5_out, or_1_out, A0);
  and and_6 (and_6_out, or_1_out, A1);
  and and_7 (and_7_out, or_1_out, A2);
  and and_8 (and_8_out, or_1_out, A3);
  and and_9 (and_9_out, or_1_out, A4);
  and and_10 (and_10_out, or_1_out, A5);
  and and_11 (and_11_out, or_1_out, A6);
  and and_12 (and_12_out, or_1_out, A7);
  and and_13 (and_13_out, or_1_out, A8);
  and and_14 (and_14_out, or_1_out, A9);
  and and_15 (and_15_out, or_1_out, A10);
  and and_16 (and_16_out, or_1_out, A11);
  and and_17 (and_17_out, and_2_out, A11);
  and and_18 (and_18_out, and_2_out, A10);
  and and_19 (and_19_out, and_2_out, A9);
  and and_20 (and_20_out, and_2_out, A8);
  and and_21 (and_21_out, and_2_out, A7);
  and and_22 (and_22_out, and_2_out, A6);
  and and_23 (and_23_out, and_2_out, A5);
  and and_24 (and_24_out, and_2_out, A4);
  and and_25 (and_25_out, and_2_out, A3);
  and and_26 (and_26_out, and_2_out, A2);
  and and_27 (and_27_out, and_2_out, A1);
  and and_28 (and_28_out, and_2_out, A0);
  and and_29 (and_29_out, and_3_out, xor_1_out);
  and and_30 (and_30_out, and_3_out, xor_2_out);
  and and_31 (and_31_out, and_3_out, xor_3_out);
  and and_32 (and_32_out, and_3_out, xor_4_out);
  and and_33 (and_33_out, and_3_out, xor_5_out);
  and and_34 (and_34_out, and_3_out, xor_6_out);
  and and_35 (and_35_out, and_3_out, xor_7_out);
  and and_36 (and_36_out, and_3_out, xor_8_out);
  and and_37 (and_37_out, and_3_out, xor_9_out);
  and and_38 (and_38_out, and_3_out, xor_10_out);
  and and_39 (and_39_out, and_3_out, xor_11_out);
  and and_40 (and_40_out, and_3_out, xor_12_out);
  or or_2 (CNT_A0, and_5_out, and_17_out, and_29_out);
  or or_3 (CNT_A1, and_6_out, and_18_out, and_30_out);
  or or_4 (CNT_A2, and_7_out, and_19_out, and_31_out);
  or or_5 (CNT_A3, and_8_out, and_20_out, and_32_out);
  or or_6 (CNT_A4, and_9_out, and_21_out, and_33_out);
  or or_7 (CNT_A5, and_10_out, and_22_out, and_34_out);
  or or_8 (CNT_A6, and_11_out, and_23_out, and_35_out);
  or or_9 (CNT_A7, and_12_out, and_24_out, and_36_out);
  or or_10 (CNT_A8, and_13_out, and_25_out, and_37_out);
  or or_11 (CNT_A9, and_14_out, and_26_out, and_38_out);
  or or_12 (CNT_A10, and_15_out, and_27_out, and_39_out);
  or or_13 (CNT_A11, and_16_out, and_28_out, and_40_out);
endmodule
